# Fritzing sketch UselessBoxes (saved by Fritzing 1.0.5)
circuit board: 8.46667cm x 5.64444cm
breadboards: 1

parts:
  Part1 = Arduino Nano (Rev3.0)
  IC1 = H-Bridge [package=THT]
  S1 = Toggle Switch [package=THT]
  S2 = SPST Switch [package=switch-spdt_kit]
  M1 = DC Motor [voltage_(max)=6V voltage_(min)=3V]
  Power_plug1 = Power plug
  R1 = Resistor [tolerance=±5% power=0.25W resistance=1k package=THT]
  R3 = Resistor [tolerance=±5% power=0.25W resistance=1k package=THT]
  R4 = Resistor [tolerance=±5% power=0.25W resistance=1k package=THT]
  R5 = Resistor [tolerance=±5% power=0.25W resistance=470 package=THT]
  R6 = Resistor [tolerance=±5% power=0.25W resistance=470 package=THT]

nets:
  GND: Part1.GND, IC1.GND4, Power_plug1.GND, R1.Pin_0, R3.Pin_0, R4.Pin_0
  N1: Part1.D2, IC1.1A, R3.Pin_1, R6.Pin_0
  N2: Part1.D3, IC1.2A, R4.Pin_1, R5.Pin_0
  N3: Part1.D4, IC1.1_2EN
  N4: Part1.D5, S2.S
  N5: Part1.3V3, S1.COM, S2.O
  N6: IC1.1Y, M1.pin_2
  N7: IC1.2Y, M1.pin_1
  N8: IC1.VCC2, IC1.VCC1, Power_plug1.VCC
  N9: S1.L1, R6.Pin_1
  N10: S1.L2, R5.Pin_1
